# Fritzing sketch board (saved by Fritzing 0.9.3b)

parts:
  S4 = SWITCH-MOMENTARY-2 [package=tactile-pth-12mm]
  Onderdeel1 = Arduino Mega 2560 (Rev3)
  S5 = SWITCH-MOMENTARY-2 [package=tactile-pth-12mm]
  S6 = SWITCH-MOMENTARY-2 [package=tactile-pth-12mm]
  S7 = SWITCH-MOMENTARY-2 [package=tactile-pth-12mm]
  S11 = SWITCH-MOMENTARY-2 [package=tactile-pth-12mm]
  S12 = SWITCH-MOMENTARY-2 [package=tactile-pth-12mm]
  S13 = SWITCH-MOMENTARY-2 [package=tactile-pth-12mm]
  S14 = SWITCH-MOMENTARY-2 [package=tactile-pth-12mm]
  R1 = Resistor [tolerance=±5% resistance=10k package=THT]
  R2 = Resistor [tolerance=±5% resistance=10k package=THT]
  S18 = SWITCH-MOMENTARY-2 [package=tactile-pth-12mm]
  S19 = SWITCH-MOMENTARY-2 [package=tactile-pth-12mm]
  S20 = SWITCH-MOMENTARY-2 [package=tactile-pth-12mm]
  S21 = SWITCH-MOMENTARY-2 [package=tactile-pth-12mm]
  S25 = SWITCH-MOMENTARY-2 [package=tactile-pth-12mm]
  S26 = SWITCH-MOMENTARY-2 [package=tactile-pth-12mm]
  S27 = SWITCH-MOMENTARY-2 [package=tactile-pth-12mm]
  S28 = SWITCH-MOMENTARY-2 [package=tactile-pth-12mm]
  S32 = SWITCH-MOMENTARY-2 [package=tactile-pth-12mm]
  S33 = SWITCH-MOMENTARY-2 [package=tactile-pth-12mm]
  S34 = SWITCH-MOMENTARY-2 [package=tactile-pth-12mm]
  S35 = SWITCH-MOMENTARY-2 [package=tactile-pth-12mm]
  S39 = SWITCH-MOMENTARY-2 [package=tactile-pth-12mm]
  S40 = SWITCH-MOMENTARY-2 [package=tactile-pth-12mm]
  S41 = SWITCH-MOMENTARY-2 [package=tactile-pth-12mm]
  S42 = SWITCH-MOMENTARY-2 [package=tactile-pth-12mm]
  S46 = SWITCH-MOMENTARY-2 [package=tactile-pth-12mm]
  S47 = SWITCH-MOMENTARY-2 [package=tactile-pth-12mm]
  S48 = SWITCH-MOMENTARY-2 [package=tactile-pth-12mm]
  S49 = SWITCH-MOMENTARY-2 [package=tactile-pth-12mm]
  R3 = Resistor [tolerance=±5% resistance=10k package=THT]
  R4 = Resistor [tolerance=±5% resistance=10k package=THT]
  R5 = Resistor [tolerance=±5% resistance=10k package=THT]
  R6 = Resistor [tolerance=±5% resistance=10k package=THT]
  R7 = Resistor [tolerance=±5% resistance=10k package=THT]

nets:
  N1: S4.1, S5.2
  N2: S4.2, Onderdeel1.A0, S11.2, S19.2, S26.2, S33.2, S40.2, S47.2
  N3: Onderdeel1.A8, S7.1, R1.Pin_0
  N4: Onderdeel1.A9, S12.1, R2.Pin_0
  N5: Onderdeel1.A10, S18.1, R3.Pin_0
  N6: Onderdeel1.A11, S25.1, R4.Pin_0
  N7: Onderdeel1.A12, S32.1, R5.Pin_0
  N8: Onderdeel1.A13, Onderdeel1.GND, R1.Pin_1, R2.Pin_1, R3.Pin_1, R4.Pin_1, R5.Pin_1, R6.Pin_1, R7.Pin_1
  N9: Onderdeel1.A1, S11.1, S14.2, S19.1, S21.2, S26.1, S28.2, S33.1, S35.2, S40.1, S42.2, S47.1, S49.2
  N10: Onderdeel1.A2, S13.2, S14.1, S20.2, S21.1, S27.2, S28.1, S34.2, S35.1, S41.2, S42.1, S48.2, S49.1
  N11: Onderdeel1.A3, S12.2, S13.1, S18.2, S20.1, S25.2, S27.1, S32.2, S34.1, S39.2, S41.1, S46.2, S48.1
  N12: S5.1, S6.2
  N13: S6.1, S7.2
  N14: S39.1, R6.Pin_0
  N15: S46.1, R7.Pin_0

// code stored in the sketch: _4BtnsMatrix.ino
// constants won't change. They're used here to 
// set pin numbers:
const int outputPin_01 = 2;
const int outputPin_02 = 3;
const int inputPin_01 = 4;
const int inputPin_02 = 5;

void setup() {
  Serial.begin(9600);
  pinMode(outputPin_01, OUTPUT);  
  pinMode(outputPin_02, OUTPUT);  
  // initialize the pushbutton pin as an input:
  pinMode(inputPin_01, INPUT);
  pinMode(inputPin_02, INPUT);
}

void loop(){
  digitalWrite(outputPin_01, HIGH);
  digitalWrite(outputPin_02, LOW);
  
  if (digitalRead(inputPin_01) == HIGH) {
    Serial.println("Button 1 pushed");
  }
  else if (digitalRead(inputPin_02) == HIGH) {
    Serial.println("Button 2 pushed");
  }
  
  delay(10);
  
  digitalWrite(outputPin_01, LOW);
  digitalWrite(outputPin_02, HIGH);
  
  if (digitalRead(inputPin_01) == HIGH) {
    Serial.println("Button 3 pushed");
  }
  else if (digitalRead(inputPin_02) == HIGH) {
    Serial.println("Button 4 pushed");
  }

  delay(10);

}
